# Fritzing sketch denemeCizim (saved by Fritzing 0.9.3b)
breadboards: 1

parts:
  U1 = RFID RC522 SIP - 8 pins [chip_label="RFID RC522" package="SIP (Single Inline) [THT]"]
  Parça1 = Arduino Uno (Rev3)
  Q1 = MOSFET-NCHANNEL [package=to220v]
  LED1 = smd LED [color="Red (633nm)" package="0805 [SMD]"]
  L1 = Solenoid
  LED2 = smd LED [color="Green (555nm)" package="0805 [SMD]"]
  R1 = Resistor [tolerance=±5% resistance=220 package="2512 [SMD]"]
  R2 = Resistor [tolerance=±5% resistance=220 package="2512 [SMD]"]
  R3 = Resistor [tolerance=±5% resistance=10 package="2512 [SMD]"]

nets:
  N1: U1.IRQ, Parça1.D10_PWM/SS
  N2: U1.NSS, Parça1.D13/SCK
  N3: U1.SCK, Parça1.D11_PWM/MOSI
  N4: U1.MOSI, Parça1.D12/MISO
  GND: U1.GND, U1.RST, Parça1.GND, Q1.S, R1.Pin_1, R2.Pin_1, R3.Pin_1
  VCC: U1.VCC, Parça1.3V3
  N5: Parça1.D2, LED1.anode
  N6: Parça1.D3_PWM, LED2.anode
  N7: Parça1.D4, Q1.G, R3.Pin_0
  N8: Parça1.VIN, L1.pin2
  N9: Q1.D, L1.pin1
  N10: LED1.cathode, R2.Pin_0
  N11: LED2.cathode, R1.Pin_0

custom parts:
  RFID RC522 SIP - 8 pins: A SIP stand-in part for RFID RC522 . With 8 pins on a 300 mil single inline package (SIP) footprint.
